# Fritzing sketch mower (saved by Fritzing 0.9.3b)
breadboards: 1

parts:
  NodeMCU_/_ESP8266 = WeMos D1 Mini
  10-pin_oben = Camdenboss CTB0158-10 [part_number=CTB0158-10 package=THT]
  10-pin_Mitte = Camdenboss CTB0158-10 [part_number=CTB0158-10 package=THT]
  U1 = Optocoupler [package=THT]
  U2 = Optocoupler [package=THT]

nets:
  N1: NodeMCU_/_ESP8266.3V3, 10-pin_oben.pin8
  N2: NodeMCU_/_ESP8266.D3, U2.Pin_3
  N3: NodeMCU_/_ESP8266.D4, U1.Pin_2
  N4: NodeMCU_/_ESP8266.G, 10-pin_oben.pin4, U1.Pin_1, U2.Pin_1
  N5: 10-pin_Mitte.pin1, U1.Pin_4
  N6: 10-pin_Mitte.pin2, U2.Pin_4
  N7: 10-pin_Mitte.pin9, U2.Pin_6
  N8: 10-pin_Mitte.pin10, U1.Pin_6
